// Logisim project DL.LAB.1.circ as structural Verilog: 1 circuit, main circuit main
module main (
  input  A,
  input  A_2,
  input  B,
  input  B_2,
  input  A_3,
  input  in_6,
  input  B_3,
  input  in_8,
  input  A_4,
  output Y_AB,
  output Y_A_prime_B_AB_prime,
  output Y_AB_AB_prime,
  output Y_A_B,
  output Y_A_prime
);

  and and_1 (Y_AB, A, B);
  or or_1 (Y_A_B, in_6, in_8);
  not not_1 (Y_A_prime, A_4);
  xor xor_1 (Y_A_prime_B_AB_prime, A_2, B_2);
  xnor xnor_1 (Y_AB_AB_prime, A_3, B_3);
endmodule
